# Fritzing sketch project (saved by Fritzing 0.9.3b)

parts:
  Squix1 = OLED 0.96" 128x64 I2C SSD1306
  WeMos_D1_Mini2 = WeMos D1 Mini
  J1 = female pin header, 7 pins [form="♀ (female)"]

nets:
  VCC: Squix1.VCC, WeMos_D1_Mini2.3V3, J1.pin1
  N1: Squix1.GND, WeMos_D1_Mini2.G, J1.pin4
  N2: Squix1.SCL, WeMos_D1_Mini2.D2
  N3: Squix1.SCA, WeMos_D1_Mini2.D1
  N4: WeMos_D1_Mini2.RX, J1.pin6

notes:
  7 Pin Header on AR750
  3V3
  SCL
  SDA
  GND
  TX
  RX
